# Fritzing sketch Eye_Of_Agamotto_Sketch (saved by Fritzing 0.8.7b)

parts:
  WS2812_LED_7_Bit = NeoPixel Jewel [part_number=2226]
  Digispark1_ATTiny85 = Digispark
  5V_2A_Battery = Battery Holders [package=lipo-1100mAh]
  Reed_Switch_(NO) = SWITCH-MOMENTARY-2 [package=reed_switch_pth]
  Tower_Pro_MG90S_Servo = Tower Pro SG90 servo [part_number=101246]

nets:
  N1: WS2812_LED_7_Bit.IN, Digispark1_ATTiny85.P1
  N2: Digispark1_ATTiny85.GND, 5V_2A_Battery.-
  N3: Digispark1_ATTiny85.VIN, 5V_2A_Battery.+
  N4: Digispark1_ATTiny85.P0, Tower_Pro_MG90S_Servo.Signal
  N5: Digispark1_ATTiny85.P2, Reed_Switch_(NO).1

custom parts:
  NeoPixel Jewel: We fit seven of our tiny 5050 (5mm x 5mm) smart RGB LEDs onto a beautiful, round PCB with mounting holes and a chainable design to create what we think is our most elegant (and evening-wear appropriate) NeoPixel board yet. Use only one microcontroller pin to control as many as you can chain together! Each LED is addressable as the driver chip is inside the LED. Each one has ~18mA constant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
  Digispark: The Digispark is an Attiny85 based microcontroller development board similar to the Arduino line, only cheaper, smaller, and a bit less powerful. With a whole host of shields to extend its functionality and the ability to use the familiar Arduino IDE the Digispark is a great way to jump into electronics, or perfect for when an Arduino is too big or too much.
  Tower Pro SG90 servo: Original file by John De Cristofaro http://www.adafruit.com/products/1449 Adafruit Feedback Servo (Small) Edited by: e-radionica.com 28/9/2015
